# Fritzing sketch piro (saved by Fritzing 0.8.7b)
breadboards: 1

parts:
  U1 = 16-Channel Relay Module [package=relay-16ch]
  U2 = MCP23017 [package="DIP (Dual Inline) [THT]"]
  Raspberry_Pi_B_rev1 = Raspberry Pi B rev2

nets:
  N1: U1.IN1, U2.GPB0
  N2: U1.IN2, U2.GPA7
  N3: U1.IN3, U2.GPB1
  N4: U1.IN4, U2.GPA6
  N5: U1.IN5, U2.GPB2
  N6: U1.IN6, U2.GPA5
  N7: U1.IN7, U2.GPB3
  N8: U1.IN8, U2.GPA4
  N9: U1.IN9, U2.GPB4
  N10: U1.IN10, U2.GPA3
  N11: U1.IN11, U2.GPB5
  N12: U1.IN12, U2.GPA2
  N13: U1.IN13, U2.GPB6
  N14: U1.IN14, U2.GPA1
  N15: U1.IN15, U2.GPB7
  N16: U1.IN16, U2.GPA0
  N17: U1.VCCOUT_5V, U2.A2, Raspberry_Pi_B_rev1.5V
  GND: U1.OUT_GND, U2.GND, U2.A0, U2.A1, U2.RST, Raspberry_Pi_B_rev1.GND
  N18: U2.CS, Raspberry_Pi_B_rev1.GPIO_2
  N19: U2.SCL, Raspberry_Pi_B_rev1.GPIO_3

custom parts:
  16-Channel Relay Module: 16 channel relay module
  MCP23017: 16 bit I/O chip controlled via I2C
